# Fritzing sketch MIDI Bass Pedal (saved by Fritzing 0.9.3b)

parts:
  Part1 = Arduino Mega ADK (Rev3)
  0 = SWITCH-MOMENTARY-2 [package=reed_switch_pth]
  1 = SWITCH-MOMENTARY-2 [package=reed_switch_pth]
  2 = SWITCH-MOMENTARY-2 [package=reed_switch_pth]
  3 = SWITCH-MOMENTARY-2 [package=reed_switch_pth]
  4 = SWITCH-MOMENTARY-2 [package=reed_switch_pth]
  5 = SWITCH-MOMENTARY-2 [package=reed_switch_pth]
  6 = SWITCH-MOMENTARY-2 [package=reed_switch_pth]
  7 = SWITCH-MOMENTARY-2 [package=reed_switch_pth]
  8 = SWITCH-MOMENTARY-2 [package=reed_switch_pth]
  9 = SWITCH-MOMENTARY-2 [package=reed_switch_pth]
  10 = SWITCH-MOMENTARY-2 [package=reed_switch_pth]
  11 = SWITCH-MOMENTARY-2 [package=reed_switch_pth]
  12 = SWITCH-MOMENTARY-2 [package=reed_switch_pth]

nets:
  N1: Part1.D23, 0.1
  N2: Part1.D25, 1.1
  N3: Part1.D27, 2.1
  N4: Part1.D29, 3.1
  N5: Part1.D31, 4.1
  N6: Part1.D33, 5.1
  N7: Part1.D35, 6.1
  N8: Part1.D37, 7.1
  N9: Part1.D39, 8.1
  N10: Part1.D41, 9.1
  N11: Part1.D43, 10.1
  N12: Part1.D45, 11.1
  N13: Part1.D47, 12.1
